// Logisim project control_logic.circ as structural Verilog: 1 circuit, main circuit control_logic
module control_logic (
  input  [31:0] inst,
  input  BrEq,
  input  BrLt,
  output PCSel,
  output RegWEn,
  output [2:0] ImmSel,
  output BrUn,
  output ASel,
  output BSel,
  output [3:0] ALUSel,
  output MemRW,
  output [1:0] WBSel
);

  wire is_R_format;
  wire [31:0] demultiplexer_1_out1;

  Comparator #(.width(7), .mode("unsigned")) comparator_1 (
    .a(inst[6:0]), .b(7'b0110011), .eq(is_R_format));  // open: gt, lt
  Demultiplexer #(.width(32), .enable("false")) demultiplexer_1 (
    .out1(demultiplexer_1_out1), .in(inst), .sel(is_R_format));  // open: out0

  // Other names for the same wires on the sheet: opcode[6:0] = inst[6:0]

  // Notes on the sheet:
  //   INPUTS to your circuit
  //   DON'T CHANGE THE LOCATIONS OF THE INPUTS AND OUTPUTS!
  //   OUTPUT from your circuit
endmodule
